// Logisim project test.circ as structural Verilog: 3 circuits, main circuit main
module main (
  input  in_1,
  input  in_2,
  input  in_3,
  input  in_4,
  input  in_5,
  input  in_6,
  input  in_7,
  input  in_8,
  input  in_9,
  input  in_10,
  input  in_11,
  output out_12,
  output out_13,
  output out_14
);

  not not_1 (out_12, in_1);
  // AND_Gate and_1 has open pins: in0=in_3, in1=in_5, out=open
  // AND_Gate and_2 has open pins: in0=in_6, in1=in_7, out=open
  // AND_Gate and_3 has open pins: in0=in_8, in1=in_10, out=open
  not not_2 (out_13, in_2);
  // AND_Gate and_4 has open pins: in0=in_4, in1=in_9, out=open

  assign out_14 = in_11;
endmodule

module test (
  input  c,
  output out_2,
  output out_3
);


  assign out_2 = c;
  assign out_3 = c;
endmodule

module Pin (
  input  in_1,
  input  in_2
);

  // AND_Gate and_1 has open pins: in0=in_1, in1=in_2, out=open
endmodule
